# Fritzing sketch audio_filter (saved by Fritzing 0.9.3b)
breadboards: 1

parts:
  U1 = 2.5mm Audio Jack [package=stereojack2.5mm_specia_pogopins]
  VCC1 = Battery block 9V
  R1 = Resistor [tolerance=±5% resistance=100 package="2512 [SMD]"]
  R2 = Resistor [tolerance=±5% resistance=10k package="2512 [SMD]"]
  D1 = Diode [package=diode-1n4148]
  Q1 = NPN-Transistor [package="TO92 [THT]"]
  R3 = Resistor [tolerance=±5% resistance=100 package="2512 [SMD]"]
  R4 = Resistor [tolerance=±5% resistance=10k package="2512 [SMD]"]
  R5 = Resistor [tolerance=±5% resistance=1k package="2512 [SMD]"]
  Q2 = PNP-Transistor [package="TO92 [THT]"]
  LED4 = LED - 3mm [color="Red (633nm)" package="3 mm [THT]"]
  LED5 = LED - 3mm [color="Red (633nm)" package="3 mm [THT]"]
  R6 = Resistor [tolerance=±5% resistance=100 package="2512 [SMD]"]
  R7 = Resistor [tolerance=±5% resistance=220 package="2512 [SMD]"]
  LED10 = LED - 3mm [color="Red (633nm)" package="3 mm [THT]"]
  LED11 = LED - 3mm [color="Red (633nm)" package="3 mm [THT]"]
  Q5 = PNP-Transistor [package="TO92 [THT]"]
  R12 = Resistor [tolerance=±5% resistance=220 package="2512 [SMD]"]
  R13 = Resistor [tolerance=±5% resistance=100 package="2512 [SMD]"]
  R14 = Resistor [tolerance=±5% resistance=220 package="2512 [SMD]"]
  R15 = Resistor [tolerance=±5% resistance=100 package="2512 [SMD]"]
  Q6 = PNP-Transistor [package="TO92 [THT]"]
  LED12 = LED - 3mm [color="Red (633nm)" package="3 mm [THT]"]
  LED13 = LED - 3mm [color="Red (633nm)" package="3 mm [THT]"]
  C1 = Electrolytic Capacitor [capacitance=10μF package="100 mil [THT, electrolytic]"]
  C2 = Electrolytic Capacitor [capacitance=47nF package="100 mil [THT, electrolytic]"]
  C6 = Electrolytic Capacitor [capacitance=470nF package="100 mil [THT, electrolytic]"]
  C7 = Electrolytic Capacitor [capacitance=10nF package="100 mil [THT, electrolytic]"]
  C8 = Electrolytic Capacitor [capacitance=1µF package="100 mil [THT, electrolytic]"]
  R16 = Resistor [tolerance=±5% resistance=2.2k package="2512 [SMD]"]

nets:
  N1: U1.SLEEVE, VCC1.-, Q1.E, R6.Pin_1, R13.Pin_1, R15.Pin_1
  N2: U1.LEFT, R3.Pin_0
  N3: U1.RIGHT, R1.Pin_0
  N4: VCC1.+, R4.Pin_1, R5.Pin_1, Q2.B, R7.Pin_1, Q5.B, R12.Pin_1, R14.Pin_1, Q6.B, C2.+, C6.+, C7.-, C7.+, C8.+, R16.Pin_0
  N5: R1.Pin_1, R3.Pin_1, C1.-
  N6: R2.Pin_0, Q1.B, C1.+
  N7: R2.Pin_1, D1.C, R4.Pin_0
  N8: Q1.C, R5.Pin_0, C2.-, C6.-, R16.Pin_1
  N9: Q2.E, R7.Pin_0
  N10: Q2.C, LED4.anode
  N11: LED4.cathode, LED5.anode
  N12: LED5.cathode, R6.Pin_0
  N13: LED10.cathode, R13.Pin_0
  N14: LED10.anode, LED11.cathode
  N15: LED11.anode, Q5.C
  N16: Q5.E, R12.Pin_0
  N17: R14.Pin_0, Q6.E
  N18: R15.Pin_0, LED12.cathode
  N19: Q6.C, LED13.anode
  N20: LED12.anode, LED13.cathode
