# Fritzing sketch led_strip (saved by Fritzing 0.9.3b)
breadboards: 1

parts:
  NEOPIXEL1 = Neopixel Strip -- Black (30/m)
  Composant1 = Arduino Nano (Rev3.0)

nets:
  GND: NEOPIXEL1.GND, Composant1.GND
  N1: NEOPIXEL1.Din, Composant1.D13/SCK
  +5V: NEOPIXEL1.+5V, Composant1.5V

custom parts:
  Neopixel Strip -- Black (30/m): These NeoPixel strips have 30 digitally-addressable pixel LEDs per meter and are very affordable and are only 12.5 mm wide, 10 mm if you remove the strip from the casing.
